# Fritzing sketch non-contact switch (saved by Fritzing 0.9.3b)
circuit board: 12.2314cm x 6.7201cm
breadboards: 1

parts:
  R1 = Resistor [tolerance=±5% resistance=220 package=THT]
  R2 = Photocell (LDR) [package=THT]
  Part1 = Arduino Mega 2560 (Rev3)
  R3 = Resistor [tolerance=±5% resistance=220 package=THT]
  LED1 = LED - 5mm [color="Red (633nm)" package="5 mm [THT]"]
  HC-SR04_Sensor_1 = HC-SR04 Ultrasonic Distance Sensor

nets:
  N1: R1.Pin_0, LED1.anode
  N2: R1.Pin_1, Part1.D12_PWM
  GND: R2.pin_0, Part1.GND, R3.Pin_1, LED1.cathode, HC-SR04_Sensor_1.GND
  N3: R2.pin_1, Part1.A0, R3.Pin_0
  N4: Part1.D11_PWM, HC-SR04_Sensor_1.ECHO
  N5: Part1.D10_PWM, HC-SR04_Sensor_1.TRIG
  5V: Part1.5V, HC-SR04_Sensor_1.VCC

// code stored in the sketch: non contact switch fritzing code.ino
#include <SR04.h>
const int trigpin =10;
const int echopin =11;
const int ledpin =12;
const int ldrpin =A0;

long duration;
int distance;

void setup() {
  Serial.begin (9600);
  pinMode(trigpin,OUTPUT);
  pinMode(echopin,INPUT);
  pinMode(ledpin,OUTPUT);
  pinMode(ldrpin,INPUT);
 
}

void loop() {
  digitalWrite(trigpin,LOW);
  delayMicroseconds(2);
  digitalWrite(trigpin,HIGH);
  delayMicroseconds(10);
  digitalWrite(trigpin,LOW);

  duration = pulseIn(echopin, HIGH);

  distance = (duration/2) / 29.1;
  
  if (distance <=15)
  
  { digitalWrite(ledpin,HIGH);
    Serial.print(distance);
    Serial.println(" cm");
    delay(30000);
  }
  
  else {
  
  digitalWrite(ledpin,LOW);
  Serial.print(distance);
  Serial.println(" cm");
  
  }
  
 int ldrStatus = analogRead(ldrpin);

 if (ldrStatus <= 10)
  {
    digitalWrite(ledpin, HIGH);
    Serial.print("Its Dark, Turn on the lights:");
    Serial.println(ldrStatus);
    delay(30000);
  }
  else
  {
    digitalWrite(ledpin, LOW);
    Serial.print("Its Bright, Turn off the lights:");
    Serial.println(ldrStatus);
  }
  
delay(500);
}
